# Fritzing sketch Schematic (saved by Fritzing 0.9.3b)

parts:
  U1 = ESP32-38PinWide [part_number=ESP32-38PinWide]
  RHT1 = Humidity and Temperature Sensor RHT03
  Part1 = Arduino Uno (Rev3) - ICSP

nets:
  N1: U1.GPIO16, Part1.D3_PWM
  N2: U1.GPIO17, Part1.D2
  VCC: RHT1.Vcc, Part1.5V
  N3: RHT1.Data-signal, Part1.A0
  N4: RHT1.GND_1, Part1.GND

notes:
  2 -> RX
  3 -> TX
  17 -> RX
  16 -> TX

custom parts:
  ESP32-38PinWide: Generic 38-Pin ESP32 with wide format (only access to one side of pins on a breadboard) based on Stephen Lilley's HiLetgo ESP-WROOM-32 ESP32 ESP-32S Development Board.
